// Logisim project ALU.circ as structural Verilog: 6 circuits, main circuit main
module main (
  input  [3:0] Left_input,
  input  [3:0] Right_input,
  input  ALU_input,
  output [3:0] Left_register,
  output [3:0] Right_register,
  output [3:0] Status,
  output [3:0] A_output
);

  wire Clock_out;
  wire [3:0] alu_1_p3, alu_1_p5;

  Clock Clock (.out(Clock_out));
  Register register_1 (.in_1(Left_input), .Clock(Clock_out), .data(Left_register));
  // ALU alu_1: pin names not known; wires that end beside it: Left_register, ALU_input, alu_1_p3, Right_register, alu_1_p5
  Register register_2 (.in_1(Right_input), .Clock(Clock_out), .data(Right_register));
  Register register_3 (.in_1(alu_1_p3), .Clock(Clock_out), .data(A_output));
  Register register_4 (.in_1(alu_1_p5), .Clock(Clock_out), .data(Status));

  // Notes on the sheet:
  //   Output register
  //   Status register
endmodule

module ALU (
  input  [3:0] Left_input,
  input  [3:0] Right_input,
  input  ALU_input,
  output [3:0] Output,
  output [3:0] Status
);

  wire adder_with_carry_in_1_carry_out, adder_with_carry_in_2_carry_out, adder_with_carry_in_3_carry_out,
       adder_with_carry_in_4_carry_out, not_1_out, not_2_out, not_3_out, not_4_out, not_5_out, xor_5_out;
  wire [3:0] xor_4_out;

  xor xor_1 (xor_4_out[3], Right_input[3], ALU_input);
  xor xor_2 (xor_4_out[2], Right_input[2], ALU_input);
  xor xor_3 (xor_4_out[1], Right_input[1], ALU_input);
  xor xor_4 (xor_4_out[0], Right_input[0], ALU_input);
  // Probe on xor_4_out
  not not_1 (not_1_out, ALU_input);
  Adder_with_carry_in adder_with_carry_in_1 (
    .bit_1(Left_input[0]), .bit_2(xor_4_out[0]), .Carry_in(ALU_input),
    .carry_out(adder_with_carry_in_1_carry_out), .sum(Output[0]));
  Adder_with_carry_in adder_with_carry_in_2 (
    .bit_1(Left_input[1]), .bit_2(xor_4_out[1]), .Carry_in(adder_with_carry_in_1_carry_out),
    .carry_out(adder_with_carry_in_2_carry_out), .sum(Output[1]));
  Adder_with_carry_in adder_with_carry_in_3 (
    .bit_1(Left_input[2]), .bit_2(xor_4_out[2]), .Carry_in(adder_with_carry_in_2_carry_out),
    .carry_out(adder_with_carry_in_3_carry_out), .sum(Output[2]));
  Adder_with_carry_in adder_with_carry_in_4 (
    .bit_1(Left_input[3]), .bit_2(xor_4_out[3]), .Carry_in(adder_with_carry_in_3_carry_out),
    .carry_out(adder_with_carry_in_4_carry_out), .sum(Output[3]));
  xor xor_5 (xor_5_out, adder_with_carry_in_3_carry_out, adder_with_carry_in_4_carry_out);
  and and_1 (Status[3], Output[3], ALU_input);
  not not_2 (not_2_out, Output[3]);
  not not_3 (not_3_out, Output[1]);
  not not_4 (not_4_out, Output[2]);
  not not_5 (not_5_out, Output[0]);
  and and_2 (Status[2], not_2_out, not_4_out, not_3_out, not_5_out);
  and and_3 (Status[1], xor_5_out, ALU_input);
  and and_4 (Status[0], adder_with_carry_in_4_carry_out, not_1_out);

  // Notes on the sheet:
  //   sum bit 0
  //   carry out
  //   sum bit 1
  //   carry out
  //   sum bit 2
  //   carry out
  //   sum bit 3
  //   carry out
  //   SIGNED OVERFLOW DETECTOR
  //   OVERFLOW DETECTOR
  //   NEGATIVE DETECTOR
  //   ZERO DETECTOR
endmodule

module Register (
  input  [3:0] in_1,
  input  Clock,
  output [3:0] data
);

  D_Flip_Flop d_ff_1 (.clk(Clock), .D(in_1[0]), .Q(data[0]));  // open: Qn, preset, en, reset
  D_Flip_Flop d_ff_2 (.clk(Clock), .D(in_1[1]), .Q(data[1]));  // open: Qn, preset, en, reset
  D_Flip_Flop d_ff_3 (.clk(Clock), .D(in_1[2]), .Q(data[2]));  // open: Qn, preset, en, reset
  D_Flip_Flop d_ff_4 (.clk(Clock), .D(in_1[3]), .Q(data[3]));  // open: Qn, preset, en, reset
endmodule

module Adder_with_carry_in (
  input  Carry_in,
  input  bit_1,
  input  bit_2,
  output sum,
  output carry_out
);

  wire and_1_out, and_2_out, and_3_out, and_4_out, and_5_out, not_1_out, not_2_out, not_3_out, xor_1_out,
       xor_2_out;

  not not_1 (not_1_out, bit_2);
  and and_1 (and_1_out, bit_2, bit_1);
  or or_1 (carry_out, and_1_out, and_2_out);
  not not_2 (not_2_out, bit_1);
  xor xor_1 (xor_1_out, bit_2, bit_1);
  and and_2 (and_2_out, xor_1_out, Carry_in);
  xor xor_2 (xor_2_out, bit_1, bit_2);
  and and_3 (and_3_out, Carry_in, bit_1, bit_2);
  and and_4 (and_4_out, Carry_in, not_2_out, not_1_out);
  not not_3 (not_3_out, Carry_in);
  and and_5 (and_5_out, not_3_out, xor_2_out);
  or or_2 (sum, and_5_out, and_3_out, and_4_out);
endmodule

module Adder_without_carry_in (
  input  in_1,
  input  in_2,
  output out_3,
  output out_4
);

  and and_1 (out_4, in_2, in_1);
  xor xor_1 (out_3, in_1, in_2);
endmodule

module Multiplexer (
  input  [3:0] in_1,
  input  [3:0] in_2,
  input  in_3,
  output [3:0] out_4
);

  wire and_1_out, and_2_out, and_3_out, and_4_out, and_5_out, and_6_out, and_7_out, and_8_out, not_1_out,
       not_2_out;

  not not_1 (not_1_out, not_2_out);
  not not_2 (not_2_out, in_3);
  and and_1 (and_1_out, in_1[0], not_1_out);
  and and_2 (and_2_out, in_1[1], not_1_out);
  and and_3 (and_3_out, in_1[2], not_1_out);
  and and_4 (and_4_out, in_1[3], not_1_out);
  and and_5 (and_5_out, in_2[0], not_2_out);
  and and_6 (and_6_out, in_2[1], not_2_out);
  and and_7 (and_7_out, in_2[2], not_2_out);
  and and_8 (and_8_out, in_2[3], not_2_out);
  or or_1 (out_4[0], and_1_out, and_5_out);
  or or_2 (out_4[1], and_2_out, and_6_out);
  or or_3 (out_4[2], and_3_out, and_7_out);
  or or_4 (out_4[3], and_4_out, and_8_out);
endmodule
