// Logisim project ControlUnit.circ as structural Verilog: 15 circuits, main circuit main
module main (
  input  [7:0] A_input,
  input  [3:0] B_input,
  input  _0___MOVE,
  input  [1:0] in_4,
  input  [1:0] in_5,
  input  [1:0] input_B___10,
  input  [3:0] C_input,
  output [7:0] Register_A,
  output [3:0] Register_B,
  output [3:0] Register_C
);

  wire and_1_out, and_2_out, and_3_out, and_4_out, and_5_out, and_6_out, and_7_out, and_8_out, and_9_out,
       and_10_out, clock_out, control_unit_1__0000, control_unit_1__0010, control_unit_1__0011,
       control_unit_1__0011_2, control_unit_1__0100, control_unit_1__0100_2, control_unit_1__0101,
       control_unit_1__0101_2, control_unit_1__0110, control_unit_1__0110_2, control_unit_1__0111,
       control_unit_1__0111_2, control_unit_1__1000, control_unit_1__1000_2, control_unit_1__1001,
       ir_register_1_opcode_output, not_1_out, not_2_out, not_3_out, opcode_step_register_1_opcode_output,
       or_1_out, or_2_out, or_3_out, or_4_out, or_7_out, or_8_out, or_9_out, or_10_out, or_11_out, or_12_out,
       or_13_out, or_14_out, Reset_step_number_out, writer_1_out_4, writer_1_out_5, writer_1_out_6,
       writer_1_out_7;
  wire [1:0] ir_register_1_out_11, ir_register_1_out_13, ir_register_1_out_15, or_6_out;
  wire [3:0] incrementer_1_output, n8_4_multiplexer_1_out_4, n8_4_multiplexer_2_out_4,
       n8_4_multiplexer_3_out_4, n8_4_multiplexer_4_out_4, n16_4_multiplexer_1_out_9,
       opcode_step_register_1_output;

  Button Reset_step_number (.out(Reset_step_number_out));
  OPCODE_STEP_register opcode_step_register_1 (
    .Clock(clock_out), .OPCODEinput(ir_register_1_opcode_output), .Input(incrementer_1_output),
    .OPCODE_output(opcode_step_register_1_opcode_output), .Output(opcode_step_register_1_output),
    .Reset_step_number(Reset_step_number_out));
  // Probe on opcode_step_register_1_opcode_output
  // Probe on opcode_step_register_1_output
  or or_1 (or_1_out, and_1_out, control_unit_1__1001, control_unit_1__1000_2, and_4_out);
  Control_Unit control_unit_1 (
    .OPCODE_input(opcode_step_register_1_opcode_output), .in_1(opcode_step_register_1_output),
    ._0000(control_unit_1__0000), ._0010(control_unit_1__0010), ._0011(control_unit_1__0011),
    ._0100(control_unit_1__0100), ._0101(control_unit_1__0101), ._0110(control_unit_1__0110),
    ._0111(control_unit_1__0111), ._1000(control_unit_1__1000), ._1001(control_unit_1__1001),
    ._0011_2(control_unit_1__0011_2), ._0100_2(control_unit_1__0100_2), ._0101_2(control_unit_1__0101_2),
    ._0110_2(control_unit_1__0110_2), ._0111_2(control_unit_1__0111_2), ._1000_2(control_unit_1__1000_2));  // open: _0001, _0010_2
  and and_1 (and_1_out, or_2_out, not_2_out);
  IR_register ir_register_1 (
    .OPCODEinput(_0___MOVE), .in_2(in_4[1]), .in_3(in_4[0]), .in_4(in_5[1]), .in_5(in_5[0]),
    .in_6(input_B___10[1]), .in_7(input_B___10[0]), .OPCODE_output(ir_register_1_opcode_output),
    .out_10(ir_register_1_out_11[1]), .out_11(ir_register_1_out_11[0]), .out_12(ir_register_1_out_13[1]),
    .out_13(ir_register_1_out_13[0]), .out_14(ir_register_1_out_15[1]), .out_15(ir_register_1_out_15[0]),
    .Clock(clock_out));
  LED DONE (.in(or_1_out));
  Incrementer incrementer_1 (
    .\input (opcode_step_register_1_output), .Reset_just_step_number(Reset_step_number_out),
    .Clock(clock_out), .Trigger(not_1_out), .\output (incrementer_1_output));
  not not_1 (not_1_out, or_1_out);
  or or_2 (or_2_out, control_unit_1__0110, control_unit_1__0101);
  or or_3 (or_3_out, control_unit_1__0110_2, control_unit_1__0100_2, control_unit_1__0100, control_unit_1__0111_2, control_unit_1__0101);
  Clock clock (.out(clock_out));
  // Probe on ir_register_1_out_11
  and and_2 (and_2_out, ir_register_1_out_11[1], or_3_out);
  or or_4 (or_4_out, control_unit_1__0010, control_unit_1__0011, control_unit_1__0101_2, control_unit_1__0110);
  and and_3 (and_3_out, control_unit_1__0100_2, and_7_out);
  and and_4 (and_4_out, control_unit_1__0110_2, and_7_out);
  // Probe on ir_register_1_out_13
  and and_5 (and_5_out, ir_register_1_out_13[1], or_4_out);
  and and_6 (and_6_out, ir_register_1_out_11[0], or_3_out);
  or or_5 (or_6_out[1], and_2_out, and_5_out, and_9_out);
  // Probe on or_6_out
  not not_2 (not_2_out, and_7_out);
  and and_7 (and_7_out, or_6_out[0], not_3_out);
  and and_8 (and_8_out, ir_register_1_out_13[0], or_4_out);
  and and_9 (and_9_out, ir_register_1_out_15[1], control_unit_1__0011_2);
  or or_6 (or_6_out[0], and_6_out, and_8_out, and_10_out);
  not not_3 (not_3_out, or_6_out[1]);
  // Probe on ir_register_1_out_15
  and and_10 (and_10_out, ir_register_1_out_15[0], control_unit_1__0011_2);
  or or_7 (or_7_out, or_4_out, control_unit_1__0011_2, control_unit_1__0111);
  _16_4_multiplexer u_16_4_multiplexer_1 (
    ._00(Register_A[7:4]), ._01(Register_A[3:0]), ._10(Register_B), ._11(Register_C), .Clock(clock_out),
    .in_7(or_6_out), .Trigger(or_7_out), .reset_to_0(control_unit_1__0111), .out_9(n16_4_multiplexer_1_out_9));
  // Probe on or_6_out
  or or_8 (or_8_out, control_unit_1__0100, control_unit_1__0111_2, and_3_out);
  _8_4_multiplexer u_8_4_multiplexer_1 (
    .in_1(B_input), .in_2(n16_4_multiplexer_1_out_9), .in_3(or_8_out), .out_4(n8_4_multiplexer_1_out_4));
  _8_4_multiplexer u_8_4_multiplexer_2 (
    .in_1(C_input), .in_2(n16_4_multiplexer_1_out_9), .in_3(or_8_out), .out_4(n8_4_multiplexer_2_out_4));
  // Probe on n16_4_multiplexer_1_out_9
  Writer writer_1 (
    .Address(or_6_out), .Trigger(or_10_out), .Set_to_00(or_9_out), .out_4(writer_1_out_4),
    .out_5(writer_1_out_5), .out_6(writer_1_out_6), .out_7(writer_1_out_7));
  or or_9 (or_9_out, and_4_out, control_unit_1__1000);
  or or_10 (or_10_out, or_8_out, and_4_out, control_unit_1__1000);
  _8_4_multiplexer u_8_4_multiplexer_3 (
    .in_1(A_input[3:0]), .in_2(n16_4_multiplexer_1_out_9), .in_3(or_8_out), .out_4(n8_4_multiplexer_3_out_4));
  _8_4_multiplexer u_8_4_multiplexer_4 (
    .in_1(A_input[7:4]), .in_2(n16_4_multiplexer_1_out_9), .in_3(or_9_out), .out_4(n8_4_multiplexer_4_out_4));
  _8_bit_register u_8_bit_register_1 (
    .in_1(n8_4_multiplexer_3_out_4), .in_2(n8_4_multiplexer_4_out_4), .Trigger_1(or_13_out),
    .Trigger_2(or_14_out), .Clock(clock_out), .out_6(Register_A[3:0]), .out_7(Register_A[7:4]));
  _4_bit_register u_4_bit_register_1 (
    .in_1(n8_4_multiplexer_1_out_4), .Trigger(or_12_out), .Clock(clock_out), .data(Register_B));
  _4_bit_register u_4_bit_register_2 (
    .in_1(n8_4_multiplexer_2_out_4), .Trigger(or_11_out), .Clock(clock_out), .data(Register_C));
  or or_11 (or_11_out, writer_1_out_7, control_unit_1__0000);
  or or_12 (or_12_out, writer_1_out_6, control_unit_1__0000);
  or or_13 (or_13_out, writer_1_out_5, control_unit_1__0000);
  or or_14 (or_14_out, writer_1_out_4, control_unit_1__0000);

  // Notes on the sheet:
  //   Instruction register
  //   MOVE x y z: moves y into x
  //   MERGE x y z: merges y and z into x or moves y into x
  //   1 = MERGE
  //   Control
  //   Unit
  //   input A = 01
  //   input C = 11
  //   Set desired starting values for registers a,b,c, and instruction register, enable clock ticking
  //   If you want to re-initialize the registers, reset the entire simulation, otherwise, reset step number to perform another instruction
  //   reader
  //   writer
  //   a
  //   b
  //   c
endmodule

module IR_register (
  input  OPCODEinput,
  input  in_2,
  input  in_3,
  input  in_4,
  input  in_5,
  input  in_6,
  input  in_7,
  input  Clock,
  output OPCODE_output,
  output out_10,
  output out_11,
  output out_12,
  output out_13,
  output out_14,
  output out_15
);

  D_Flip_Flop d_ff_1 (.clk(Clock), .D(OPCODEinput), .Q(OPCODE_output));  // open: Qn, preset, en, reset
  D_Flip_Flop d_ff_2 (.clk(Clock), .D(in_2), .Q(out_10));  // open: Qn, preset, en, reset
  D_Flip_Flop d_ff_3 (.clk(Clock), .D(in_3), .Q(out_11));  // open: Qn, preset, en, reset
  D_Flip_Flop d_ff_4 (.clk(Clock), .D(in_4), .Q(out_12));  // open: Qn, preset, en, reset
  D_Flip_Flop d_ff_5 (.clk(Clock), .D(in_5), .Q(out_13));  // open: Qn, preset, en, reset
  D_Flip_Flop d_ff_6 (.clk(Clock), .D(in_6), .Q(out_14));  // open: Qn, preset, en, reset
  D_Flip_Flop d_ff_7 (.clk(Clock), .D(in_7), .Q(out_15));  // open: Qn, preset, en, reset

  // Notes on the sheet:
  //   OPCODE INPUT:
  //   0 = MOVE
  //   1 = MERGE
  //   REGISTERS:
  //   01 = Ra
  //   10 = Rb
  //   11 = Rc
endmodule

module _2_bit_register (
  input  [1:0] in_1,
  input  Clock,
  output [1:0] data
);

  D_Flip_Flop d_ff_1 (.clk(Clock), .D(in_1[0]), .Q(data[0]));  // open: Qn, preset, en, reset
  D_Flip_Flop d_ff_2 (.clk(Clock), .D(in_1[1]), .Q(data[1]));  // open: Qn, preset, en, reset
endmodule

module _4_bit_register (
  input  [3:0] in_1,
  input  Trigger,
  input  Clock,
  output [3:0] data
);

  D_Flip_Flop d_ff_1 (.clk(Clock), .D(in_1[0]), .Q(data[0]), .en(Trigger));  // open: Qn, preset, reset
  D_Flip_Flop d_ff_2 (.clk(Clock), .D(in_1[1]), .Q(data[1]), .en(Trigger));  // open: Qn, preset, reset
  D_Flip_Flop d_ff_3 (.clk(Clock), .D(in_1[2]), .Q(data[2]), .en(Trigger));  // open: Qn, preset, reset
  D_Flip_Flop d_ff_4 (.clk(Clock), .D(in_1[3]), .Q(data[3]), .en(Trigger));  // open: Qn, preset, reset
endmodule

module _8_bit_register (
  input  [3:0] in_1,
  input  [3:0] in_2,
  input  Clock,
  input  Trigger_1,
  input  Trigger_2,
  output [3:0] out_6,
  output [3:0] out_7
);

  D_Flip_Flop d_ff_1 (.clk(Clock), .D(in_1[0]), .Q(out_6[0]), .en(Trigger_1));  // open: Qn, preset, reset
  D_Flip_Flop d_ff_2 (.clk(Clock), .D(in_1[1]), .Q(out_6[1]), .en(Trigger_1));  // open: Qn, preset, reset
  D_Flip_Flop d_ff_3 (.clk(Clock), .D(in_1[2]), .Q(out_6[2]), .en(Trigger_1));  // open: Qn, preset, reset
  D_Flip_Flop d_ff_4 (.clk(Clock), .D(in_1[3]), .Q(out_6[3]), .en(Trigger_1));  // open: Qn, preset, reset
  D_Flip_Flop d_ff_5 (.clk(Clock), .D(in_2[0]), .Q(out_7[0]), .en(Trigger_2));  // open: Qn, preset, reset
  D_Flip_Flop d_ff_6 (.clk(Clock), .D(in_2[1]), .Q(out_7[1]), .en(Trigger_2));  // open: Qn, preset, reset
  D_Flip_Flop d_ff_7 (.clk(Clock), .D(in_2[2]), .Q(out_7[2]), .en(Trigger_2));  // open: Qn, preset, reset
  D_Flip_Flop d_ff_8 (.clk(Clock), .D(in_2[3]), .Q(out_7[3]), .en(Trigger_2));  // open: Qn, preset, reset

  // Notes on the sheet:
  //   bits 0-3
  //   bits 4-7
endmodule

module OPCODE_STEP_register (
  input  OPCODEinput,
  input  [3:0] Input,
  input  Clock,
  input  Reset_step_number,
  output [3:0] Output,
  output OPCODE_output
);

  _1_bit_register u_1_bit_register_1 (.Clock(Clock), .OPCODEinput(OPCODEinput), .out_3(OPCODE_output));
  _4_bit_register_with_reset u_4_bit_register_with_reset_1 (
    .Clock(Clock), .in_2(Input), .data(Output), .reset_step_number_but_not_registers(Reset_step_number));  // open: Trigger

  // Notes on the sheet:
  //   OPCODE INPUT:
  //   0 = MOVE
  //   1 = MERGE
endmodule

module Control_Unit (
  input  [3:0] in_1,
  input  OPCODE_input,
  output _0000,
  output _0001,
  output _0010,
  output _0011,
  output _0100,
  output _0101,
  output _0110,
  output _0111,
  output _1000,
  output _1001,
  output _0010_2,
  output _0011_2,
  output _0100_2,
  output _0101_2,
  output _0110_2,
  output _0111_2,
  output _1000_2
);

  wire and_1_out, and_12_out, and_13_out, and_14_out, and_22_out, and_23_out, and_24_out, and_25_out,
       and_26_out, not_1_out, not_2_out, not_3_out, not_4_out, not_5_out, not_6_out, not_7_out, not_8_out,
       not_9_out, not_10_out, not_11_out, not_12_out, not_13_out, not_14_out, not_15_out, not_16_out,
       not_17_out, not_18_out, not_19_out, not_20_out, not_21_out, not_22_out, not_23_out, not_24_out,
       not_25_out, not_26_out, not_27_out, not_28_out, not_29_out, not_30_out, not_31_out, not_32_out,
       not_33_out, not_34_out, not_35_out, not_36_out, not_37_out, not_38_out, not_39_out, not_40_out,
       not_41_out, not_42_out, not_43_out, not_44_out, not_45_out, not_46_out, not_47_out, not_48_out,
       not_49_out, not_50_out, not_51_out;

  not not_1 (not_1_out, OPCODE_input);
  buf and_1 (and_1_out, OPCODE_input);  // AND_Gate
  not not_2 (not_2_out, in_1[0]);
  not not_3 (not_3_out, in_1[1]);
  not not_4 (not_4_out, in_1[2]);
  not not_5 (not_5_out, in_1[3]);
  not not_6 (not_6_out, in_1[1]);
  not not_7 (not_7_out, in_1[2]);
  not not_8 (not_8_out, in_1[3]);
  not not_9 (not_9_out, in_1[0]);
  not not_10 (not_10_out, in_1[2]);
  not not_11 (not_11_out, in_1[2]);
  not not_12 (not_12_out, in_1[0]);
  not not_13 (not_13_out, in_1[1]);
  not not_14 (not_14_out, in_1[1]);
  not not_15 (not_15_out, in_1[0]);
  not not_16 (not_16_out, in_1[3]);
  not not_17 (not_17_out, in_1[0]);
  not not_18 (not_18_out, in_1[1]);
  not not_19 (not_19_out, in_1[2]);
  not not_20 (not_20_out, in_1[1]);
  not not_21 (not_21_out, in_1[2]);
  not not_22 (not_22_out, in_1[0]);
  not not_23 (not_23_out, in_1[2]);
  not not_24 (not_24_out, in_1[2]);
  not not_25 (not_25_out, in_1[1]);
  not not_26 (not_26_out, in_1[2]);
  not not_27 (not_27_out, in_1[3]);
  not not_28 (not_28_out, in_1[0]);
  not not_29 (not_29_out, in_1[2]);
  not not_30 (not_30_out, in_1[3]);
  not not_31 (not_31_out, in_1[2]);
  not not_32 (not_32_out, in_1[3]);
  not not_33 (not_33_out, in_1[0]);
  not not_34 (not_34_out, in_1[1]);
  not not_35 (not_35_out, in_1[3]);
  not not_36 (not_36_out, in_1[1]);
  not not_37 (not_37_out, in_1[3]);
  not not_38 (not_38_out, in_1[0]);
  not not_39 (not_39_out, in_1[3]);
  not not_40 (not_40_out, in_1[3]);
  not not_41 (not_41_out, in_1[0]);
  not not_42 (not_42_out, in_1[1]);
  not not_43 (not_43_out, in_1[2]);
  not not_44 (not_44_out, in_1[1]);
  not not_45 (not_45_out, in_1[2]);
  not not_46 (not_46_out, in_1[0]);
  not not_47 (not_47_out, in_1[2]);
  not not_48 (not_48_out, in_1[2]);
  not not_49 (not_49_out, in_1[0]);
  not not_50 (not_50_out, in_1[1]);
  not not_51 (not_51_out, in_1[1]);
  and and_2 (_0000, not_2_out, not_3_out, not_4_out, not_5_out);
  and and_3 (_0001, in_1[0], not_6_out, not_7_out, not_8_out);
  and and_4 (_0010, not_1_out, not_9_out, in_1[1], not_10_out);
  and and_5 (_0011, not_1_out, in_1[0], in_1[1], not_11_out);
  and and_6 (_0100, not_1_out, not_12_out, not_13_out, in_1[2]);
  and and_7 (_0101, not_1_out, in_1[0], not_14_out, in_1[2]);
  and and_8 (_0110, not_1_out, not_15_out, in_1[1], in_1[2]);
  and and_9 (_0111, not_1_out, in_1[0], in_1[1], in_1[2], not_16_out);
  and and_10 (_1000, not_1_out, not_17_out, not_18_out, not_19_out, in_1[3]);
  and and_11 (_1001, not_1_out, in_1[0], not_20_out, not_21_out, in_1[3]);
  and and_12 (and_12_out, not_1_out, not_22_out, in_1[1], not_23_out, in_1[3]);
  and and_13 (and_13_out, not_1_out, in_1[0], in_1[1], not_24_out, in_1[3]);
  and and_14 (and_14_out, and_1_out, in_1[0], not_25_out, not_26_out, not_27_out);
  and and_15 (_0010_2, and_1_out, not_28_out, in_1[1], not_29_out, not_30_out);
  and and_16 (_0011_2, and_1_out, in_1[0], in_1[1], not_31_out, not_32_out);
  and and_17 (_0100_2, and_1_out, not_33_out, not_34_out, in_1[2], not_35_out);
  and and_18 (_0101_2, and_1_out, in_1[0], not_36_out, in_1[2], not_37_out);
  and and_19 (_0110_2, and_1_out, not_38_out, in_1[1], in_1[2], not_39_out);
  and and_20 (_0111_2, and_1_out, in_1[0], in_1[1], in_1[2], not_40_out);
  and and_21 (_1000_2, and_1_out, not_41_out, not_42_out, not_43_out, in_1[3]);
  and and_22 (and_22_out, and_1_out, in_1[0], not_44_out, not_45_out, in_1[3]);
  and and_23 (and_23_out, and_1_out, not_46_out, in_1[1], not_47_out, in_1[3]);
  and and_24 (and_24_out, and_1_out, in_1[0], in_1[1], not_48_out, in_1[3]);
  and and_25 (and_25_out, and_1_out, not_49_out, not_50_out, in_1[2], in_1[3]);
  and and_26 (and_26_out, and_1_out, in_1[0], not_51_out, in_1[2], in_1[3]);

  // Notes on the sheet:
  //   this trigger is for initializing the registers
  //   This trigger is for loading the OPCODE
  //   This trigger is for loading the OPCODE
endmodule

module Incrementer (
  input  Reset_just_step_number,
  input  [3:0] \input ,
  input  Clock,
  input  Trigger,
  output [3:0] \output 
);

  wire [3:0] n4_bit_register_with_reset_1_data;

  _4_bit_register_with_reset u_4_bit_register_with_reset_1 (
    .Clock(Clock), .Trigger(Trigger), .in_2(\input ), .data(n4_bit_register_with_reset_1_data),
    .reset_step_number_but_not_registers(Reset_just_step_number));
  // Probe on n4_bit_register_with_reset_1_data
  // Probe on \output 
  Adder #(.width(4)) adder_1 (
    .a(n4_bit_register_with_reset_1_data), .b(4'b0000), .out(\output ), .cin(1'b1));  // open: cout
endmodule

module _1_bit_register (
  input  OPCODEinput,
  input  Clock,
  output out_3
);

  D_Flip_Flop d_ff_1 (.clk(Clock), .D(OPCODEinput), .Q(out_3));  // open: Qn, preset, en, reset
endmodule

module _8_4_multiplexer (
  input  [3:0] in_1,
  input  [3:0] in_2,
  input  in_3,
  output [3:0] out_4
);

  wire and_1_out, and_2_out, and_3_out, and_4_out, and_5_out, and_6_out, and_7_out, and_8_out, not_1_out;

  not not_1 (not_1_out, in_3);
  and and_1 (and_1_out, in_1[0], not_1_out);
  and and_2 (and_2_out, in_1[1], not_1_out);
  and and_3 (and_3_out, in_1[2], not_1_out);
  and and_4 (and_4_out, in_1[3], not_1_out);
  and and_5 (and_5_out, in_2[0], in_3);
  and and_6 (and_6_out, in_2[1], in_3);
  and and_7 (and_7_out, in_2[2], in_3);
  and and_8 (and_8_out, in_2[3], in_3);
  or or_1 (out_4[0], and_1_out, and_5_out);
  or or_2 (out_4[1], and_2_out, and_6_out);
  or or_3 (out_4[2], and_3_out, and_7_out);
  or or_4 (out_4[3], and_4_out, and_8_out);
endmodule

module _16_4_multiplexer (
  input  Clock,
  input  Trigger,
  input  [3:0] _00,
  input  [3:0] _01,
  input  [3:0] _10,
  input  [3:0] _11,
  input  [1:0] in_7,
  input  reset_to_0,
  output [3:0] out_9
);

  wire and_1_out, and_2_out, not_1_out;
  wire [3:0] n8_4_multiplexer_1_out_4, n8_4_multiplexer_2_out_4, n8_4_multiplexer_3_out_4;

  and and_1 (and_1_out, in_7[1], not_1_out);
  _8_4_multiplexer u_8_4_multiplexer_1 (.in_1(_00), .in_2(_01), .in_3(and_2_out), .out_4(n8_4_multiplexer_1_out_4));
  _8_4_multiplexer u_8_4_multiplexer_2 (.in_1(_10), .in_2(_11), .in_3(and_2_out), .out_4(n8_4_multiplexer_2_out_4));
  and and_2 (and_2_out, in_7[0], not_1_out);
  not not_1 (not_1_out, reset_to_0);
  _8_4_multiplexer u_8_4_multiplexer_3 (
    .in_1(n8_4_multiplexer_1_out_4), .in_2(n8_4_multiplexer_2_out_4), .in_3(and_1_out),
    .out_4(n8_4_multiplexer_3_out_4));
  // Probe on n8_4_multiplexer_3_out_4
  Reader reader_1 (.in_3(n8_4_multiplexer_3_out_4), .trigger(Trigger), .clock(Clock), .data(out_9));
endmodule

module Reader (
  input  trigger,
  input  clock,
  input  [3:0] in_3,
  output [3:0] data
);

  D_Flip_Flop d_ff_1 (.clk(clock), .D(in_3[0]), .Q(data[0]), .en(trigger));  // open: Qn, preset, reset
  D_Flip_Flop d_ff_2 (.clk(clock), .D(in_3[1]), .Q(data[1]), .en(trigger));  // open: Qn, preset, reset
  D_Flip_Flop d_ff_3 (.clk(clock), .D(in_3[2]), .Q(data[2]), .en(trigger));  // open: Qn, preset, reset
  D_Flip_Flop d_ff_4 (.clk(clock), .D(in_3[3]), .Q(data[3]), .en(trigger));  // open: Qn, preset, reset
endmodule

module Writer (
  input  [1:0] Address,
  input  Trigger,
  input  Set_to_00,
  output out_4,
  output out_5,
  output out_6,
  output out_7
);

  wire _00_out, _01_out, _10_out, _11_out, and_1_out, and_2_out, and_3_out, and_4_out, not_1_out, not_2_out,
       not_3_out, not_4_out, not_5_out;

  and _01 (_01_out, Address[0], not_1_out);
  not not_1 (not_1_out, Address[1]);
  not not_2 (not_2_out, Address[0]);
  and _10 (_10_out, not_2_out, Address[1]);
  and _11 (_11_out, Address[0], Address[1]);
  nor _00 (_00_out, Address[0], Address[1]);
  and and_1 (and_1_out, Trigger, _00_out);
  and and_2 (and_2_out, Trigger, _01_out);
  and and_3 (and_3_out, Trigger, _10_out);
  and and_4 (and_4_out, Trigger, _11_out);
  or or_1 (out_4, and_1_out, Set_to_00);
  and and_5 (out_5, and_2_out, not_3_out);
  not not_3 (not_3_out, Set_to_00);
  and and_6 (out_6, and_3_out, not_4_out);
  not not_4 (not_4_out, Set_to_00);
  and and_7 (out_7, and_4_out, not_5_out);
  not not_5 (not_5_out, Set_to_00);
endmodule

module _4_bit_register_with_reset (
  input  reset_step_number_but_not_registers,
  input  [3:0] in_2,
  input  Clock,
  input  Trigger,
  output [3:0] data
);

  D_Flip_Flop d_ff_1 (
    .clk(Clock), .D(in_2[0]), .Q(data[0]), .preset(reset_step_number_but_not_registers), .en(Trigger));  // open: Qn, reset
  D_Flip_Flop d_ff_2 (
    .clk(Clock), .D(in_2[1]), .Q(data[1]), .en(Trigger), .reset(reset_step_number_but_not_registers));  // open: Qn, preset
  D_Flip_Flop d_ff_3 (
    .clk(Clock), .D(in_2[2]), .Q(data[2]), .en(Trigger), .reset(reset_step_number_but_not_registers));  // open: Qn, preset
  D_Flip_Flop d_ff_4 (
    .clk(Clock), .D(in_2[3]), .Q(data[3]), .en(Trigger), .reset(reset_step_number_but_not_registers));  // open: Qn, preset
endmodule

module New_Incrementer (
  input  [3:0] \input ,
  input  Reset_just_step_number,
  input  Clock,
  input  Trigger,
  output [3:0] \output 
);

  wire and_1_out, and_2_out, and_3_out, and_4_out;
  wire [3:0] undriven;

  and and_1 (and_1_out, \input [1], Trigger);
  and and_2 (and_2_out, \input [3], Trigger);
  and and_3 (and_3_out, \input [2], Trigger);
  and and_4 (and_4_out, \input [0], Trigger);
  // Probe on undriven
  // Probe on \output 
  Adder #(.width(4)) adder_1 (.a(undriven), .b(4'b0000), .out(\output ), .cin(1'b1));  // open: cout
endmodule
