// Logisim project RAM_memory.circ as structural Verilog: 9 circuits, main circuit main
module main (
  input  [1:0] Address,
  input  [3:0] Data,
  input  in_3,
  output [3:0] Output,
  output [3:0] out_5,
  output [3:0] out_6,
  output [3:0] out_7,
  output [3:0] out_8
);

  wire clock_1_out;

  Clock clock_1 (.out(clock_1_out));
  RAM ram_1 (
    .Address(Address), .Clock(clock_1_out), .data(Data), .mode(in_3), .out_7(Output), ._00(out_5),
    ._01(out_6), ._10(out_7), ._11(out_8));

  // Notes on the sheet:
  //   Clock
  //   RAM
  //   Mode (1=write,0=read)
endmodule

module nibble (
  input  address,
  input  mode,
  input  [3:0] in_3,
  output [3:0] data
);

  wire and_1_out;

  and and_1 (and_1_out, address, mode);
  D_Flip_Flop d_ff_1 (.clk(and_1_out), .D(in_3[0]), .Q(data[0]));  // open: Qn, preset, en, reset
  D_Flip_Flop d_ff_2 (.clk(and_1_out), .D(in_3[1]), .Q(data[1]));  // open: Qn, preset, en, reset
  D_Flip_Flop d_ff_3 (.clk(and_1_out), .D(in_3[2]), .Q(data[2]));  // open: Qn, preset, en, reset
  D_Flip_Flop d_ff_4 (.clk(and_1_out), .D(in_3[3]), .Q(data[3]));  // open: Qn, preset, en, reset
endmodule

module _2_1_multiplexer (
  input  bit0,
  input  bit1,
  input  sel,
  output out
);

  wire and_1_out, and_2_out, not_1_out;

  not not_1 (not_1_out, sel);
  and and_1 (and_1_out, bit0, not_1_out);
  and and_2 (and_2_out, bit1, sel);
  or or_1 (out, and_1_out, and_2_out);
endmodule

module _4_2_multiplexer (
  input  [1:0] in_1,
  input  [1:0] in_2,
  input  in_3,
  output [1:0] out_4
);

  _2_1_multiplexer u_2_1_multiplexer_1 (.bit0(in_1[0]), .bit1(in_2[0]), .sel(in_3), .out(out_4[0]));
  _2_1_multiplexer u_2_1_multiplexer_2 (.bit0(in_1[1]), .bit1(in_2[1]), .sel(in_3), .out(out_4[1]));
endmodule

module _8_4_multiplexer (
  input  [3:0] in_1,
  input  [3:0] in_2,
  input  in_3,
  output [3:0] out_4
);

  _4_2_multiplexer u_4_2_multiplexer_1 (.in_1(in_1[1:0]), .in_2(in_2[1:0]), .in_3(in_3), .out_4(out_4[1:0]));
  _4_2_multiplexer u_4_2_multiplexer_2 (.in_1(in_1[3:2]), .in_2(in_2[3:2]), .in_3(in_3), .out_4(out_4[3:2]));
endmodule

module _16_4_multiplexer_reader (
  input  [3:0] _00,
  input  Mode,
  input  Clock,
  input  [3:0] _01,
  input  [3:0] _10,
  input  [3:0] _11,
  input  [1:0] in_7,
  output [3:0] out_8
);

  wire [3:0] n8_4_multiplexer_1_out_4, n8_4_multiplexer_2_out_4, n8_4_multiplexer_3_out_4;

  _8_4_multiplexer u_8_4_multiplexer_1 (.in_1(_00), .in_2(_01), .in_3(in_7[0]), .out_4(n8_4_multiplexer_1_out_4));
  _8_4_multiplexer u_8_4_multiplexer_2 (.in_1(_10), .in_2(_11), .in_3(in_7[0]), .out_4(n8_4_multiplexer_2_out_4));
  _8_4_multiplexer u_8_4_multiplexer_3 (
    .in_1(n8_4_multiplexer_1_out_4), .in_2(n8_4_multiplexer_2_out_4), .in_3(in_7[1]),
    .out_4(n8_4_multiplexer_3_out_4));
  Reader reader_1 (.in_3(n8_4_multiplexer_3_out_4), .trigger(Mode), .clock(Clock), .data(out_8));
endmodule

module RAM (
  input  Clock,
  input  mode,
  input  [3:0] data,
  input  [1:0] Address,
  output [3:0] _00,
  output [3:0] _01,
  output [3:0] out_7,
  output [3:0] _10,
  output [3:0] _11
);

  wire decoder_1_out_3, decoder_1_out_4, decoder_1_out_5, decoder_1_out_6;

  Decoder decoder_1 (
    .Address(Address), .Clock(Clock), .out_3(decoder_1_out_3), .out_4(decoder_1_out_4),
    .out_5(decoder_1_out_5), .out_6(decoder_1_out_6));
  nibble nibble_1 (.in_3(data), .address(decoder_1_out_3), .mode(mode), .data(_00));
  nibble nibble_2 (.in_3(data), .address(decoder_1_out_4), .mode(mode), .data(_01));
  nibble nibble_3 (.in_3(data), .address(decoder_1_out_5), .mode(mode), .data(_10));
  nibble nibble_4 (.in_3(data), .address(decoder_1_out_6), .mode(mode), .data(_11));
  _16_4_multiplexer_reader u_16_4_multiplexer_reader_1 (
    ._00(_00), ._01(_01), ._10(_10), ._11(_11), .Mode(mode), .Clock(Clock), .in_7(Address), .out_8(out_7));

  // Notes on the sheet:
  //   decoder
  //   multiplexer
endmodule

module Decoder (
  input  [1:0] Address,
  input  Clock,
  output out_3,
  output out_4,
  output out_5,
  output out_6
);

  wire _00_out, _01_out, _10_out, _11_out, not_1_out, not_2_out;

  and _01 (_01_out, Address[0], not_1_out);
  not not_1 (not_1_out, Address[1]);
  not not_2 (not_2_out, Address[0]);
  and _10 (_10_out, not_2_out, Address[1]);
  and _11 (_11_out, Address[0], Address[1]);
  nor _00 (_00_out, Address[0], Address[1]);
  and and_1 (out_3, Clock, _00_out);
  and and_2 (out_4, Clock, _01_out);
  and and_3 (out_5, Clock, _10_out);
  and and_4 (out_6, Clock, _11_out);
endmodule

module Reader (
  input  trigger,
  input  clock,
  input  [3:0] in_3,
  output [3:0] data
);

  wire and_1_out, not_1_out;

  not not_1 (not_1_out, trigger);
  and and_1 (and_1_out, clock, not_1_out);
  D_Flip_Flop d_ff_1 (.clk(and_1_out), .D(in_3[0]), .Q(data[0]));  // open: Qn, preset, en, reset
  D_Flip_Flop d_ff_2 (.clk(and_1_out), .D(in_3[1]), .Q(data[1]));  // open: Qn, preset, en, reset
  D_Flip_Flop d_ff_3 (.clk(and_1_out), .D(in_3[2]), .Q(data[2]));  // open: Qn, preset, en, reset
  D_Flip_Flop d_ff_4 (.clk(and_1_out), .D(in_3[3]), .Q(data[3]));  // open: Qn, preset, en, reset
endmodule
