// Logisim project RSflipflop.circ as structural Verilog: 1 circuit, main circuit main
module main (
  input  R,
  input  S,
  output Q,
  output out_4
);

  wire and_1_out, and_2_out, clock_1_out;

  Clock clock_1 (.out(clock_1_out));
  and and_1 (and_1_out, R, clock_1_out);
  and and_2 (and_2_out, clock_1_out, S);
  nor nor_1 (Q, and_1_out, out_4);
  nor nor_2 (out_4, Q, and_2_out);
endmodule
